# Fritzing sketch ColorCompass (saved by Fritzing 0.9.3b)
breadboards: 1

parts:
  Part2 = LSM303 Breakout Board - Tilt-Compensated Compass
  Part1 = Arduino Uno (Rev3)
  LED1 = RGB LED (com. cathode, rgb) [package="5 mm [THT]"]

nets:
  GND: Part2.GND, Part1.GND, LED1.common_cathode
  N1: Part1.D9_PWM, LED1.blue_anode
  N2: Part1.D10_PWM/SS, LED1.green_anode
  N3: Part1.D11_PWM/MOSI, LED1.red_anode
